// Logisim project Micro_Parcial_2_Ej_1_Kevin_Gonzalez.circ as structural Verilog: 9 circuits, main circuit RippleCarryAdder
module RippleCarryAdder (
  input  A,
  input  B,
  input  Cin,
  output S,
  output Cout
);

  wire and_1_out, and_2_out, xor_1_out;

  xor xor_1 (xor_1_out, A, B);
  and and_1 (and_1_out, Cin, xor_1_out);
  and and_2 (and_2_out, A, B);
  xor xor_2 (S, xor_1_out, Cin);
  or or_1 (Cout, and_1_out, and_2_out);
endmodule

module RippleCaryAdder_main (
  input  [3:0] A,
  input  [3:0] B,
  input  Cin,
  output [3:0] S,
  output Cout
);

  wire ripplecarryadder_1_cout, ripplecarryadder_2_cout, ripplecarryadder_3_cout;

  RippleCarryAdder ripplecarryadder_1 (.A(A[0]), .B(B[0]), .Cin(Cin), .S(S[0]), .Cout(ripplecarryadder_1_cout));
  RippleCarryAdder ripplecarryadder_2 (
    .A(A[1]), .B(B[1]), .Cin(ripplecarryadder_1_cout), .S(S[1]), .Cout(ripplecarryadder_2_cout));
  RippleCarryAdder ripplecarryadder_3 (
    .A(A[2]), .B(B[2]), .Cin(ripplecarryadder_2_cout), .S(S[2]), .Cout(ripplecarryadder_3_cout));
  RippleCarryAdder ripplecarryadder_4 (.A(A[3]), .B(B[3]), .Cin(ripplecarryadder_3_cout), .S(S[3]), .Cout(Cout));
endmodule

module CarryLookaheadAdder_CarryGenerator (
  input  [3:0] P,
  input  [3:0] G,
  input  Cin,
  output [4:0] C
);

  wire and_1_out, and_2_out, and_3_out, and_4_out, and_5_out, and_6_out, and_7_out, and_8_out, and_9_out,
       and_10_out, and_11_out, and_12_out, and_13_out, and_14_out, and_15_out, and_16_out, and_17_out,
       and_18_out, and_19_out, and_20_out, or_1_out, or_2_out, or_3_out, or_4_out, or_5_out, or_7_out;

  and and_1 (and_1_out, Cin, P[0]);
  and and_2 (and_2_out, P[1], P[2]);
  and and_3 (and_3_out, G[0], P[1]);
  and and_4 (and_4_out, P[2], P[3]);
  and and_5 (and_5_out, G[1], P[2]);
  and and_6 (and_6_out, G[2], P[3]);
  and and_7 (and_7_out, Cin, P[0]);
  and and_8 (and_8_out, P[1], P[2]);
  and and_9 (and_9_out, G[0], P[1]);
  and and_10 (and_10_out, G[1], P[2]);
  and and_11 (and_11_out, P[1], P[0]);
  and and_12 (and_12_out, P[1], G[0]);
  and and_13 (and_13_out, P[0], Cin);
  and and_14 (and_14_out, and_2_out, P[3]);
  and and_15 (and_15_out, and_3_out, and_4_out);
  and and_16 (and_16_out, and_5_out, P[3]);
  and and_17 (and_17_out, and_7_out, and_8_out);
  and and_18 (and_18_out, and_9_out, P[2]);
  and and_19 (and_19_out, and_11_out, Cin);
  and and_20 (and_20_out, and_1_out, and_14_out);
  or or_1 (or_1_out, and_20_out, and_15_out);
  or or_2 (or_2_out, and_6_out, G[3]);
  or or_3 (or_3_out, and_17_out, and_18_out);
  or or_4 (or_4_out, and_10_out, G[2]);
  or or_5 (or_5_out, and_19_out, and_12_out);
  or or_6 (C[4], and_13_out, G[0]);
  or or_7 (or_7_out, or_1_out, and_16_out);
  or or_8 (C[2], or_3_out, or_4_out);
  or or_9 (C[3], or_5_out, G[1]);
  or or_10 (C[1], or_7_out, or_2_out);

  assign C[0] = Cin;

  // Other names for the same wires on the sheet: C3 = C[1]; C1 = C[3]; C0 = C[4]
endmodule

module CarryLookaheadAdder_P_and_G (
  input  [3:0] A,
  input  [3:0] B,
  output [3:0] P,
  output [3:0] G
);

  xor xor_1 (P[0], A[0], B[0]);
  and and_1 (G[0], A[0], B[0]);
  xor xor_2 (P[1], A[1], B[1]);
  and and_2 (G[1], A[1], B[1]);
  xor xor_3 (P[2], A[2], B[2]);
  and and_3 (G[2], A[2], B[2]);
  xor xor_4 (P[3], A[3], B[3]);
  and and_4 (G[3], A[3], B[3]);
endmodule

module CarryLookaheadAdder_main (
  input  [3:0] A,
  input  [3:0] B,
  input  Cin,
  output [4:0] out_4
);

  wire [3:0] carrylookaheadadder_carrygenerator_1_c, carrylookaheadadder_p_and_g_1_g,
       carrylookaheadadder_p_and_g_1_p;

  CarryLookaheadAdder_P_and_G carrylookaheadadder_p_and_g_1 (
    .A(A), .B(B), .P(carrylookaheadadder_p_and_g_1_p), .G(carrylookaheadadder_p_and_g_1_g));
  CarryLookaheadAdder_CarryGenerator carrylookaheadadder_carrygenerator_1 (
    .P(carrylookaheadadder_p_and_g_1_p), .G(carrylookaheadadder_p_and_g_1_g), .Cin(Cin),
    .C({out_4[4], carrylookaheadadder_carrygenerator_1_c}));
  xor xor_1 (out_4[0], carrylookaheadadder_p_and_g_1_p[0], carrylookaheadadder_carrygenerator_1_c[0]);
  xor xor_2 (out_4[1], carrylookaheadadder_p_and_g_1_p[1], carrylookaheadadder_carrygenerator_1_c[1]);
  xor xor_3 (out_4[2], carrylookaheadadder_p_and_g_1_p[2], carrylookaheadadder_carrygenerator_1_c[2]);
  xor xor_4 (out_4[3], carrylookaheadadder_p_and_g_1_p[3], carrylookaheadadder_carrygenerator_1_c[3]);
endmodule

module PrefixAdder_main (
  input  [3:0] A,
  input  [3:0] B,
  input  Cin,
  output [3:0] out_4,
  output out_5
);

  wire [3:0] prefixadder_inputpg_1_g1, prefixadder_inputpg_1_p1, prefixadder_outputpg_1_g2;

  PrefixAdder_InputPG prefixadder_inputpg_1 (
    .A(A), .B(B), .G1(prefixadder_inputpg_1_g1), .P1(prefixadder_inputpg_1_p1));
  PrefixAdder_OutputPG prefixadder_outputpg_1 (
    .G1(prefixadder_inputpg_1_g1), .Cin(Cin), .P1(prefixadder_inputpg_1_p1), .G2(prefixadder_outputpg_1_g2),
    .Cout(out_5));
  PrefixAdder_Final prefixadder_final_1 (.G2(prefixadder_outputpg_1_g2), .A(A), .B(B), .S(out_4));
endmodule

module PrefixAdder_InputPG (
  input  [3:0] A,
  input  [3:0] B,
  output [3:0] G1,
  output [3:0] P1
);

  and and_1 (G1[0], A[0], B[0]);
  or or_1 (P1[0], A[0], B[0]);
  and and_2 (G1[1], A[1], B[1]);
  or or_2 (P1[1], A[1], B[1]);
  and and_3 (G1[2], A[2], B[2]);
  or or_3 (P1[2], A[2], B[2]);
  and and_4 (G1[3], A[3], B[3]);
  or or_4 (P1[3], A[3], B[3]);
endmodule

module PrefixAdder_Final (
  input  [3:0] G2,
  input  [3:0] A,
  input  [3:0] B,
  output [3:0] S
);

  wire xor_1_out, xor_2_out, xor_3_out, xor_4_out;

  xor xor_1 (xor_1_out, G2[0], A[0]);
  xor xor_2 (xor_2_out, G2[1], A[1]);
  xor xor_3 (xor_3_out, G2[2], A[2]);
  xor xor_4 (xor_4_out, G2[3], A[3]);
  xor xor_5 (S[0], xor_1_out, B[0]);
  xor xor_6 (S[1], xor_2_out, B[1]);
  xor xor_7 (S[2], xor_3_out, B[2]);
  xor xor_8 (S[3], xor_4_out, B[3]);
endmodule

module PrefixAdder_OutputPG (
  input  [3:0] G1,
  input  Cin,
  input  [3:0] P1,
  output [3:0] G2,
  output Cout
);

  wire and_1_out, and_2_out, and_3_out, and_4_out, and_5_out, and_6_out, and_7_out, and_8_out, and_9_out,
       and_10_out, and_12_out, and_13_out, and_14_out, and_15_out, or_2_out, or_3_out, or_4_out, or_8_out,
       undriven, undriven_4;
  wire [3:0] undriven_2, undriven_3;

  and and_1 (and_1_out, Cin, P1[0]);
  and and_2 (and_2_out, G1[1], P1[2]);
  and and_3 (and_3_out, P1[1], P1[2]);
  or or_1 (G2[1], and_1_out, G1[0]);
  or or_2 (or_2_out, and_2_out, G1[2]);
  and and_4 (and_4_out, undriven, undriven_2[0]);
  and and_5 (and_5_out, undriven_4, undriven_2[0]);
  and and_6 (and_6_out, undriven_3[1], undriven_2[2]);
  and and_7 (and_7_out, undriven_2[1], undriven_2[2]);
  and and_8 (and_8_out, G2[1], P1[1]);
  and and_9 (and_9_out, G2[1], and_3_out);
  or or_3 (or_3_out, and_4_out, undriven_3[0]);
  or or_4 (or_4_out, and_6_out, undriven_3[2]);
  or or_5 (G2[2], and_8_out, G1[1]);
  or or_6 (G2[3], and_9_out, or_2_out);
  and and_10 (and_10_out, or_3_out, undriven_2[1]);
  // AND_Gate and_11 has open pins: in0=and_5_out, in1=undriven_2[1], out=open
  and and_12 (and_12_out, or_3_out, and_7_out);
  and and_13 (and_13_out, and_5_out, and_7_out);
  and and_14 (and_14_out, G2[3], P1[3]);
  // OR_Gate or_7 has open pins: in0=and_10_out, in1=undriven_3[1], out=open
  or or_8 (or_8_out, and_12_out, or_4_out);
  or or_9 (Cout, and_14_out, G1[3]);
  and and_15 (and_15_out, or_8_out, undriven_2[3]);
  // AND_Gate and_16 has open pins: in0=and_13_out, in1=undriven_2[3], out=open
  // OR_Gate or_10 has open pins: in0=and_15_out, in1=undriven_3[3], out=open

  assign G2[0] = Cin;
endmodule
