// Logisim project Micro_Parcial_2_Ej_2.1_Kevin_Gonzalez.circ as structural Verilog: 10 circuits, main circuit ALU4
module ALU4 (
  input  [1:0] OP,
  input  [6:0] A,
  input  [6:0] B,
  output [6:0] Resultado,
  output Cero,
  output Neg,
  output CarryOP,
  output Overflow
);

  wire Cout, not_1_out, not_3_out, Overflow_t, Resta;
  wire [6:0] multiplexer_1_out, not_2_out, op_add_sub_1_sum, op_and_1_and2, op_or_1_or2;

  not not_1 (not_1_out, OP[1]);
  assign not_2_out = ~B;  // NOT_Gate not_2, 7 bits wide
  and and_1 (Resta, OP[0], not_1_out);
  Multiplexer #(.width(7)) multiplexer_1 (.in0(B), .in1(not_2_out), .out(multiplexer_1_out), .sel(Resta));
  not not_3 (not_3_out, Resta);
  and and_2 (CarryOP, Cout, not_3_out);
  and and_3 (Overflow, Overflow_t, Resta);
  OP_ADD_SUB op_add_sub_1 (
    .Resta(Resta), .A(A), .B(multiplexer_1_out), .Sum(op_add_sub_1_sum), .Cero(Cero), .Neg(Neg), .Cout(Cout),
    .Overflow(Overflow_t));
  OP_AND op_and_1 (.A(A), .B(B), .AND2(op_and_1_and2));
  OP_OR op_or_1 (.A(A), .B(B), .OR2(op_or_1_or2));
  Multiplexer #(.select(2), .width(7)) multiplexer_2 (
    .in0(op_add_sub_1_sum), .in1(op_add_sub_1_sum), .in2(op_and_1_and2), .in3(op_or_1_or2), .out(Resultado),
    .sel(OP));
endmodule

module FullAdder (
  input  A,
  input  B,
  input  Cin,
  output S,
  output Cout
);

  wire and_1_out, and_2_out, xor_1_out;

  xor xor_1 (xor_1_out, A, B);
  xor xor_2 (S, xor_1_out, Cin);
  and and_1 (and_1_out, Cin, xor_1_out);
  and and_2 (and_2_out, A, B);
  or or_1 (Cout, and_1_out, and_2_out);
endmodule

module OP_AND (
  input  [6:0] A,
  input  [6:0] B,
  output [6:0] AND2
);

  assign AND2 = A & B;  // AND_Gate and_1, 7 bits wide
endmodule

module OP_OR (
  input  [6:0] A,
  input  [6:0] B,
  output [6:0] OR2
);

  assign OR2 = A | B;  // OR_Gate or_1, 7 bits wide
endmodule

module OP_ADD_SUB (
  input  Resta,
  input  [6:0] A,
  input  [6:0] B,
  output [6:0] Sum,
  output Cero,
  output Neg,
  output Cout,
  output Overflow
);

  wire C5, fulladder_1_cout, fulladder_2_cout, fulladder_3_cout, fulladder_4_cout, fulladder_5_cout, or_1_out;

  FullAdder fulladder_1 (.A(A[0]), .B(B[0]), .Cin(Resta), .S(Sum[0]), .Cout(fulladder_1_cout));
  FullAdder fulladder_2 (.A(A[1]), .B(B[1]), .Cin(fulladder_1_cout), .S(Sum[1]), .Cout(fulladder_2_cout));
  FullAdder fulladder_3 (.A(A[2]), .B(B[2]), .Cin(fulladder_2_cout), .S(Sum[2]), .Cout(fulladder_3_cout));
  FullAdder fulladder_4 (.A(A[3]), .B(B[3]), .Cin(fulladder_3_cout), .S(Sum[3]), .Cout(fulladder_4_cout));
  FullAdder fulladder_5 (.A(A[4]), .B(B[4]), .Cin(fulladder_4_cout), .S(Sum[4]), .Cout(fulladder_5_cout));
  FullAdder fulladder_6 (.A(A[5]), .B(B[5]), .Cin(fulladder_5_cout), .S(Sum[5]), .Cout(C5));
  FullAdder fulladder_7 (.A(A[6]), .B(B[6]), .Cin(C5), .S(Sum[6]), .Cout(Cout));
  xor xor_1 (Overflow, C5, Cout);
  or or_1 (or_1_out, Sum[0], Sum[1], Sum[2], Sum[3], Sum[4], Sum[5], Sum[6]);
  not not_1 (Cero, or_1_out);
  and and_1 (Neg, Sum[6], Resta);

  // Other names for the same wires on the sheet: C6 = Cout; S0 = Sum[0]; S1 = Sum[1]; S2 = Sum[2]; S3 = Sum[3];
  //   S4 = Sum[4]; S5 = Sum[5]; S6 = Sum[6]
endmodule

module ShiftLeft (
  input  [6:0] A,
  output [6:0] ShiftL,
  output Carry
);


  assign Carry = A[6];
  assign ShiftL = {A[5:0], A[6]};
endmodule

module ShiftRight (
  input  [6:0] A,
  output [6:0] ShiftR,
  output Carry
);


  assign Carry = A[0];
  assign ShiftR = {A[0], A[6:1]};
endmodule

module ALU6_FINAL (
  input  [3:0] OP,
  input  [6:0] A,
  input  [6:0] B,
  output [6:0] out_4,
  output [6:0] out_5
);

  wire alu6_1_carryop, alu6_1_carryshift, alu6_1_cero, alu6_1_neg, alu6_1_overflow;

  ALU6 alu6_1 (
    .OP(OP), .A(A), .B(B), .Shift(out_4), .CarryShift(alu6_1_carryshift), .Resultado(out_5),
    .Cero(alu6_1_cero), .Neg(alu6_1_neg), .CarryOP(alu6_1_carryop), .Overflow(alu6_1_overflow));
  LED led_1 (.in(alu6_1_carryshift));
  LED led_2 (.in(alu6_1_cero));
  LED led_3 (.in(alu6_1_neg));
  LED led_4 (.in(alu6_1_carryop));
  LED led_5 (.in(alu6_1_overflow));
endmodule

module ALU6 (
  input  [3:0] OP,
  input  [6:0] A,
  input  [6:0] B,
  output [6:0] Shift,
  output CarryShift,
  output [6:0] Resultado,
  output Cero,
  output Neg,
  output CarryOP,
  output Overflow
);

  wire Cout, not_1_out, not_3_out, Overflow_t, Resta, shiftleft_1_carry, shiftright_1_carry;
  wire [6:0] multiplexer_1_out, not_2_out, op_add_sub_1_sum, op_and_1_and2, op_or_1_or2, shiftleft_1_shiftl,
       shiftright_1_shiftr;

  not not_1 (not_1_out, OP[1]);
  assign not_2_out = ~B;  // NOT_Gate not_2, 7 bits wide
  and and_1 (Resta, OP[0], not_1_out);
  Multiplexer #(.width(7)) multiplexer_1 (.in0(B), .in1(not_2_out), .out(multiplexer_1_out), .sel(Resta));
  not not_3 (not_3_out, Resta);
  and and_2 (CarryOP, Cout, not_3_out);
  and and_3 (Overflow, Overflow_t, Resta);
  ShiftRight shiftright_1 (.A(A), .ShiftR(shiftright_1_shiftr), .Carry(shiftright_1_carry));
  ShiftLeft shiftleft_1 (.A(A), .ShiftL(shiftleft_1_shiftl), .Carry(shiftleft_1_carry));
  OP_ADD_SUB op_add_sub_1 (
    .Resta(Resta), .A(Shift), .B(multiplexer_1_out), .Sum(op_add_sub_1_sum), .Cero(Cero), .Neg(Neg),
    .Cout(Cout), .Overflow(Overflow_t));
  OP_AND op_and_1 (.A(Shift), .B(B), .AND2(op_and_1_and2));
  OP_OR op_or_1 (.A(Shift), .B(B), .OR2(op_or_1_or2));
  Multiplexer #(.select(2), .width(7)) multiplexer_2 (
    .in0(A), .in1(shiftright_1_shiftr), .in2(shiftleft_1_shiftl), .out(Shift), .sel(OP[3:2]));  // open: in3
  or or_1 (CarryShift, shiftright_1_carry, shiftleft_1_carry);
  Multiplexer #(.select(2), .width(7)) multiplexer_3 (
    .in0(op_add_sub_1_sum), .in1(op_add_sub_1_sum), .in2(op_and_1_and2), .in3(op_or_1_or2), .out(Resultado),
    .sel(OP[1:0]));

  // Other names for the same wires on the sheet: OP_t[1:0] = OP[1:0]; OP2[1:0] = OP[3:2]
endmodule

module ALU4_FINAL (
  input  [1:0] OP,
  input  [6:0] A,
  input  [6:0] B,
  output [6:0] out_4
);

  wire alu4_1_carryop, alu4_1_cero, alu4_1_neg, alu4_1_overflow;

  ALU4 alu4_1 (
    .OP(OP), .A(A), .B(B), .Resultado(out_4), .Cero(alu4_1_cero), .Neg(alu4_1_neg), .CarryOP(alu4_1_carryop),
    .Overflow(alu4_1_overflow));
  LED led_1 (.in(alu4_1_cero));
  LED led_2 (.in(alu4_1_neg));
  LED led_3 (.in(alu4_1_carryop));
  LED led_4 (.in(alu4_1_overflow));
endmodule
